# Fritzing sketch Raspberry-Pi-Circut (saved by Fritzing 0.9.10b)
breadboards: 1

parts:
  S1 = Pushbutton [package="[THT]"]
  S2 = Pushbutton [package="[THT]"]
  S3 = Pushbutton [package="[THT]"]
  S4 = Pushbutton [package="[THT]"]
  Mod1 = Raspberry Pi 4B

nets:
  N1: S1.Pin_1, S1.Pin_2
  N2: S1.Pin_3, S1.Pin_4, S2.Pin_3, S2.Pin_4, S3.Pin_3, S3.Pin_4, S4.Pin_3, S4.Pin_4
  N3: S2.Pin_1, S2.Pin_2
  N4: S3.Pin_1, S3.Pin_2
  N5: S4.Pin_1, S4.Pin_2, Mod1.GPIO21
